// Digital circuit 5 bit_Register_Set.dig as structural Verilog
module _5_bit_Register_Set (
  input  [4:0] WRD_4_0,
  input  [1:0] WR_1_0,
  input  CLK,
  input  WE,
  input  [1:0] RA_1_0,
  input  [1:0] RB_1_0,
  output [4:0] A_4_0,
  output [4:0] B_4_0
);

  wire A0, A1, A2, A3, D0, D1, D2, D3;
  wire [4:0] R0, R1, R2, R3;

  and and_1 (D1, WE, A1);
  and and_2 (D0, WE, A0);
  Decoder #(.Selector_Bits(2)) decoder_1 (.sel(WR_1_0), .out_0(A0), .out_1(A1), .out_2(A2), .out_3(A3));
  and and_3 (D3, WE, A3);
  and and_4 (D2, WE, A2);
  _5_bit_Reg _5_bit_reg_1 (.Din_4_0(WRD_4_0), .Sel(D3), .CLK(CLK), .Dout_4_0(R3));
  _5_bit_Reg _5_bit_reg_2 (.Din_4_0(WRD_4_0), .Sel(D2), .CLK(CLK), .Dout_4_0(R2));
  _5_bit_Reg _5_bit_reg_3 (.Din_4_0(WRD_4_0), .Sel(D1), .CLK(CLK), .Dout_4_0(R1));
  _5_bit_Reg _5_bit_reg_4 (.Din_4_0(WRD_4_0), .Sel(D0), .CLK(CLK), .Dout_4_0(R0));
  Multiplexer #(.Selector_Bits(2), .Bits(5)) multiplexer_1 (
    .sel(RB_1_0), .in_0(R3), .in_1(R2), .in_2(R1), .in_3(R0), .out(B_4_0));
  Multiplexer #(.Selector_Bits(2), .Bits(5)) multiplexer_2 (
    .sel(RA_1_0), .in_0(R3), .in_1(R2), .in_2(R1), .in_3(R0), .out(A_4_0));
  // _5_bit_Register_Set _5_bit_register_set_1: pin names not known
endmodule
